# Fritzing sketch Air_Quality_ESP8266 (saved by Fritzing 0.9.3b)
breadboards: 1

parts:
  TFT2 = Color 320x240 TFT Display, ILI9341 Controller Chip
  U6 = ESP8266 NodeMCU LoLin module
  Mod2 = KY-015 Temperature & Humidity Sensor Module [package="Breakout board"]
  YF-S201_Flow_Meter2 = YF-S201 Water Flow Meter
  VCC1 = Battery
  U7 = Hirose DF13 Series Header [part_number=DF13A-6P-1.25H package=DF13A-6P-1.25H]
  Part3 = MQ-7 breakout

nets:
  VCC: TFT2.VCC, TFT2.LED, TFT2.SDO_(MISO), U6.3V3, Mod2.Vin
  GND: TFT2.GND, U6.GND, Mod2.-, YF-S201_Flow_Meter2.GND, VCC1.-, U7.2, Part3.GND
  N1: TFT2.CS, U6.D2
  N2: TFT2.Reset, TFT2.D/C, U6.D3
  N3: TFT2.SDI_(MOSI), U6.D7
  N4: TFT2.SCK, U6.D5
  N5: U6.D1, Mod2.S
  N6: U6.RX, U7.6
  N7: U6.TX, U7.5
  VCC_2: U6.Vin, YF-S201_Flow_Meter2.VCC, VCC1.+, U7.1, Part3.VCC
  N8: U6.A0, Part3.AO

notes:
  3.3 V rail ( from ESP8266 )
  5 V rail (external power supply )

custom parts:
  Color 320x240 TFT Display, ILI9341 Controller Chip: 2.2" TFT Display with ILI9341 Controller
  ESP8266 NodeMCU LoLin module: ESP8266 based NodeMCU
  KY-015 Temperature & Humidity Sensor Module: KY-015 temperature and humidity sensor module, provides a low-latency serial interface to measure humidity and temperature.
  YF-S201 Water Flow Meter: The YF-S201 Flow Meter. The input voltage is 5V to 24V (DC).
  Battery: Your standard 2x 18650 battery pack (7,4 Volts)
  MQ-7 breakout: SKU: 101282
