# Fritzing sketch Air_Quality_Sensor (saved by Fritzing 0.9.3b)
breadboards: 1

parts:
  U1 = ESP8266 NodeMCU LoLin module
  Mod1 = KY-015 Temperature & Humidity Sensor Module [package="Breakout board"]
  Part1 = MQ-7 breakout
  U5 = Hirose DF13 Series Header [part_number=DF13A-6P-1.25H package=DF13A-6P-1.25H]
  TFT1 = Color 320x240 TFT Display, ILI9341 Controller Chip
  YF-S201_Flow_Meter1 = YF-S201 Water Flow Meter
  Part2 = Analog Digital MUX Breakout
  Grove1 = Grove OLED 128x96

nets:
  N1: U1.D0, Part2.S0
  N2: U1.D1, Part2.S1, Grove1.SCL
  N3: U1.D2, Part2.S2, Grove1.SDA
  N4: U1.D3, Part2.S3
  GND: U1.GND, Mod1.-, Part1.GND, U5.2, YF-S201_Flow_Meter1.GND, Part2.GND, Part2.EN, Grove1.GND
  N5: U1.D8, Mod1.S
  N6: U1.RX, U5.5
  N7: U1.TX, U5.6
  VCC: U1.3V3, Mod1.Vin, Part2.VCC, Grove1.VCC
  VCC_2: U1.Vin, Part1.VCC, U5.1, YF-S201_Flow_Meter1.VCC
  N8: U1.A0, Part2.SIG
  N9: Part1.AO, Part2.C15
  N10: TFT1.Reset, TFT1.D/C
  N11: TFT1.LED, TFT1.SDO_(MISO)
  N12: YF-S201_Flow_Meter1.SIG, Part2.C14

custom parts:
  ESP8266 NodeMCU LoLin module: ESP8266 based NodeMCU
  KY-015 Temperature & Humidity Sensor Module: KY-015 temperature and humidity sensor module, provides a low-latency serial interface to measure humidity and temperature.
  MQ-7 breakout: SKU: 101282
  Color 320x240 TFT Display, ILI9341 Controller Chip: 2.2" TFT Display with ILI9341 Controller
  YF-S201 Water Flow Meter: The YF-S201 Flow Meter. The input voltage is 5V to 24V (DC).
