# Fritzing sketch Humidity_and_Air_Quality (saved by Fritzing 0.9.3b)
breadboards: 1

parts:
  U6 = ESP8266 NodeMCU LoLin module
  Mod2 = KY-015 Temperature & Humidity Sensor Module [package="Breakout board"]
  U7 = Hirose DF13 Series Header [part_number=DF13A-6P-1.25H package=DF13A-6P-1.25H]

nets:
  N1: U6.GND, Mod2.-, U7.2
  N2: U6.D8, Mod2.S
  N3: U6.RX, U7.5
  N4: U6.TX, U7.6
  3V3: U6.3V3, Mod2.Vin
  N5: U6.Vin, U7.1

custom parts:
  ESP8266 NodeMCU LoLin module: ESP8266 based NodeMCU
  KY-015 Temperature & Humidity Sensor Module: KY-015 temperature and humidity sensor module, provides a low-latency serial interface to measure humidity and temperature.
